# Fritzing sketch OPAMP+EmitterFollower+R (saved by Fritzing 0.9.3b)
breadboards: 1

parts:
  IC1 = Dual Op-Amp [package=dip08]
  C1 = Ceramic Capacitor [capacitance=100nF package="100 mil [THT, multilayer]"]
  C2 = Ceramic Capacitor [capacitance=100nF package="100 mil [THT, multilayer]"]
  R1 = Resistor [tolerance=±5% resistance=10k package=THT]
  Q1 = NPN-Transistor [package="TO92 [THT]"]
  R2 = Resistor [tolerance=±5% resistance=100 package=THT]
  R3 = Resistor [tolerance=±5% resistance=1k package=THT]
  R4 = Resistor [tolerance=±5% resistance=1k package=THT]
  C3 = Ceramic Capacitor [capacitance=100nF package="100 mil [THT, multilayer]"]
  R5 = Resistor [tolerance=±5% resistance=4.7k package=THT]
  C4 = Electrolytic Capacitor [capacitance=1µF package="100 mil [THT, electrolytic]"]
  C5 = Electrolytic Capacitor [capacitance=1µF package="100 mil [THT, electrolytic]"]
  R6 = Resistor [tolerance=±5% resistance=200 package=THT]
  C6 = Ceramic Capacitor [capacitance=100nF package="100 mil [THT, multilayer]"]

nets:
  N1: IC1.A_OUT, R6.Pin_0
  N2: IC1.A_-IN, R4.Pin_0, C3.1, R5.Pin_1
  N3: IC1.A_+IN, IC1.B_+IN, C1.0, C2.1, R1.Pin_0, R1.Pin_1, Q1.E, R2.Pin_0, R3.Pin_0, R3.Pin_1, R4.Pin_1, C3.0, R5.Pin_0, C4.-, C5.+, C6.1
  N4: IC1.A_V-, C2.0, R2.Pin_1, C5.-
  N5: IC1.B_-IN, IC1.B_OUT
  N6: IC1.A_V+, C1.1, Q1.B, C4.+, C6.0
  N7: Q1.C, R6.Pin_1

notes:
  GND
  +4.5V
  -4.5V
  GND
  IN
  OUT
