# Fritzing sketch OPAMP+PushPull (saved by Fritzing 0.9.3b)
breadboards: 1

parts:
  IC1 = Dual Op-Amp [package=dip08]
  D1 = Rectifier Diode [part_number=1N4001 package="300 mil [THT]"]
  D2 = Rectifier Diode [part_number=1N4001 package="300 mil [THT]"]
  R1 = Resistor [tolerance=±5% resistance=6.8k package=THT]
  Q1 = PNP-Transistor [package="TO92 [THT]"]
  R2 = Resistor [tolerance=±5% resistance=33 package=THT]
  D3 = Rectifier Diode [part_number=1N4001 package="300 mil [THT]"]
  D4 = Rectifier Diode [part_number=1N4001 package="300 mil [THT]"]
  Q2 = NPN-Transistor [package="TO92 [THT]"]
  R3 = Resistor [tolerance=±5% resistance=6.8k package=THT]
  R4 = Resistor [tolerance=±5% resistance=33 package=THT]
  R5 = Resistor [tolerance=±5% resistance=1k package=THT]
  R6 = Resistor [tolerance=±5% resistance=3.3k package=THT]
  C1 = Ceramic Capacitor [capacitance=100nF package="100 mil [THT, multilayer]"]
  C2 = Ceramic Capacitor [capacitance=100nF package="100 mil [THT, multilayer]"]
  R7 = Resistor [tolerance=±5% resistance=100 package=THT]
  C3 = Ceramic Capacitor [capacitance=100nF package="100 mil [THT, multilayer]"]
  R8 = Resistor [tolerance=±5% resistance=22k package=THT]
  C4 = Electrolytic Capacitor [capacitance=1µF package="100 mil [THT, electrolytic]"]
  C5 = Electrolytic Capacitor [capacitance=1µF package="100 mil [THT, electrolytic]"]
  C6 = Ceramic Capacitor [capacitance=100nF package="100 mil [THT, multilayer]"]
  C7 = Ceramic Capacitor [capacitance=100nF package="100 mil [THT, multilayer]"]

nets:
  N1: IC1.A_OUT, D1.anode, D3.cathode
  N2: IC1.A_-IN, R5.Pin_0, R6.Pin_1, C3.0
  N3: IC1.A_+IN, R8.Pin_0
  N4: IC1.A_V-, R1.Pin_1, Q1.B, C2.0, C5.-, C6.1
  N5: IC1.B_+IN, R5.Pin_1, C1.0, C2.1, R7.Pin_1, R8.Pin_1, C4.-, C5.+, C6.0, C7.1
  N6: IC1.B_-IN, IC1.B_OUT
  N7: IC1.A_V+, Q2.B, R3.Pin_0, C1.1, C4.+, C7.0
  N8: D1.cathode, D2.anode
  N9: D2.cathode, R1.Pin_0, Q1.C
  N10: Q1.E, R2.Pin_1
  N11: R2.Pin_0, R4.Pin_0, R6.Pin_0, R7.Pin_0, C3.1
  N12: D3.anode, D4.cathode
  N13: D4.anode, Q2.C, R3.Pin_1
  N14: Q2.E, R4.Pin_1

notes:
  -4.5V
  GND
  GND
  +4.5V
  OUT
  IN
