# Fritzing sketch Emitter_Follower_ConstantCurrent (saved by Fritzing 0.9.3b)
breadboards: 1

parts:
  Q1 = NPN-Transistor [package="TO92 [THT]"]
  R1 = Resistor [tolerance=±5% resistance=15k package=THT]
  R2 = Resistor [tolerance=±5% resistance=12k package=THT]
  C2 = Electrolytic Capacitor [capacitance=1µF package="100 mil [THT, electrolytic]"]
  C3 = Electrolytic Capacitor [capacitance=1µF package="100 mil [THT, electrolytic]"]
  C4 = Ceramic Capacitor [capacitance=100nF package="100 mil [THT, multilayer]"]
  C5 = Electrolytic Capacitor [capacitance=1µF package="100 mil [THT, electrolytic]"]
  R5 = Resistor [tolerance=±5% resistance=200 package=THT]
  Q2 = NPN-Transistor [package="TO92 [THT]"]
  R6 = Resistor [tolerance=±5% resistance=150 package=THT]
  R7 = Resistor [tolerance=±5% resistance=3.3k package=THT]
  R8 = Resistor [tolerance=±5% resistance=12k package=THT]

nets:
  N1: Q1.E, C2.+, Q2.B
  N2: Q1.B, R2.Pin_0, C4.0, C5.+, R8.Pin_1
  N3: Q1.C, R1.Pin_0, R2.Pin_1, C3.+
  N4: R1.Pin_1, C4.1, C5.-, R5.Pin_1, R6.Pin_1, R7.Pin_1
  N5: C2.-, R5.Pin_0
  N6: Q2.E, R6.Pin_0
  N7: Q2.C, R7.Pin_0, R8.Pin_0

notes:
  IN
  OUT
  GND
  +9V
