# Fritzing sketch Emitter_Follower (saved by Fritzing 0.9.3b)
breadboards: 1

parts:
  Q1 = NPN-Transistor [package="TO92 [THT]"]
  R1 = Resistor [tolerance=±5% resistance=10k package=THT]
  R2 = Resistor [tolerance=±5% resistance=10k package=THT]
  R3 = Resistor [tolerance=±5% resistance=200 package=THT]
  C2 = Electrolytic Capacitor [capacitance=1µF package="100 mil [THT, electrolytic]"]
  C3 = Electrolytic Capacitor [capacitance=1µF package="100 mil [THT, electrolytic]"]
  R4 = Resistor [tolerance=±5% resistance=200 package=THT]
  C4 = Ceramic Capacitor [capacitance=100nF package="100 mil [THT, multilayer]"]
  C5 = Electrolytic Capacitor [capacitance=1µF package="100 mil [THT, electrolytic]"]
  R5 = Resistor [tolerance=±5% resistance=1k package=THT]

nets:
  N1: Q1.E, C2.+, R4.Pin_0
  N2: Q1.B, R2.Pin_0, C4.0, C5.+
  N3: Q1.C, R1.Pin_0, R2.Pin_1, C3.+
  N4: R1.Pin_1, R3.Pin_1, C4.1, C5.-, R5.Pin_1
  N5: R3.Pin_0, R4.Pin_1
  N6: C2.-, R5.Pin_0

notes:
  IN
  OUT
  GND
  +9V
  GND
  NC
