# Fritzing sketch Emitter__Common+Emitter_Follower_DeCoupling  (saved by Fritzing 0.9.3b)
breadboards: 1

parts:
  Q1 = NPN-Transistor [package="TO92 [THT]"]
  R1 = Resistor [tolerance=±5% resistance=27k package=THT]
  R2 = Resistor [tolerance=±5% resistance=68k package=THT]
  C2 = Electrolytic Capacitor [capacitance=1µF package="100 mil [THT, electrolytic]"]
  C3 = Electrolytic Capacitor [capacitance=1µF package="100 mil [THT, electrolytic]"]
  R4 = Resistor [tolerance=±5% resistance=470 package=THT]
  C4 = Ceramic Capacitor [capacitance=100nF package="100 mil [THT, multilayer]"]
  C5 = Electrolytic Capacitor [capacitance=1µF package="100 mil [THT, electrolytic]"]
  Q2 = NPN-Transistor [package="TO92 [THT]"]
  R5 = Resistor [tolerance=±5% resistance=12k package=THT]
  R6 = Resistor [tolerance=±5% resistance=12k package=THT]
  R7 = Resistor [tolerance=±5% resistance=2k package=THT]
  C6 = Ceramic Capacitor [capacitance=100nF package="100 mil [THT, multilayer]"]
  R8 = Resistor [tolerance=±5% resistance=470 package=THT]

nets:
  N1: Q1.E, C2.+, R4.Pin_0, C4.0
  N2: Q1.B, R2.Pin_0, C5.+, R5.Pin_0, R6.Pin_0, C6.1
  N3: R1.Pin_0, R2.Pin_1, C3.+, Q2.C
  N4: R1.Pin_1, R4.Pin_1, C4.1, C5.-, R7.Pin_1, C6.0, R8.Pin_1
  N5: C2.-, R8.Pin_0
  N6: Q2.E, R7.Pin_0
  N7: Q2.B, R5.Pin_1, R6.Pin_1

notes:
  IN
  OUT
  GND
  +9V
  GND
  NC
