# Fritzing sketch Emitter_Common (saved by Fritzing 0.9.3b)
breadboards: 1

parts:
  Q1 = NPN-Transistor [package="TO92 [THT]"]
  R1 = Resistor [tolerance=±5% resistance=27k package=THT]
  R2 = Resistor [tolerance=±5% resistance=68k package=THT]
  R3 = Resistor [tolerance=±5% resistance=2k package=THT]
  C2 = Electrolytic Capacitor [capacitance=1µF package="100 mil [THT, electrolytic]"]
  R4 = Resistor [tolerance=±5% resistance=12k package=THT]
  C3 = Electrolytic Capacitor [capacitance=1µF package="100 mil [THT, electrolytic]"]
  R5 = Resistor [tolerance=±5% resistance=12k package=THT]

nets:
  N1: Q1.E, R3.Pin_0
  N2: Q1.B, C2.+, R4.Pin_1, R5.Pin_1
  N3: Q1.C, R1.Pin_0, R2.Pin_1, C3.+
  N4: R1.Pin_1, R3.Pin_1
  N5: R2.Pin_0, R4.Pin_0, R5.Pin_0

notes:
  IN
  OUT
  NC
  +9V
  GND
  NC
