# Fritzing sketch Cascode_BootStrap (saved by Fritzing 0.9.3b)
breadboards: 1

parts:
  Q1 = NPN-Transistor [package="TO92 [THT]"]
  Q2 = NPN-Transistor [package="TO92 [THT]"]
  R1 = Resistor [tolerance=±5% resistance=3.3k package=THT]
  D1 = Rectifier Diode [part_number=1N4001 package="300 mil [THT]"]
  R2 = Resistor [tolerance=±5% resistance=15k package=THT]
  C1 = Electrolytic Capacitor [capacitance=1µF package="100 mil [THT, electrolytic]"]
  R3 = Resistor [tolerance=±5% resistance=15k package=THT]
  R4 = Resistor [tolerance=±5% resistance=3.3k package=THT]
  R5 = Resistor [tolerance=±5% resistance=680 package=THT]
  C2 = Electrolytic Capacitor [capacitance=1µF package="100 mil [THT, electrolytic]"]
  C3 = Ceramic Capacitor [capacitance=100nF package="100 mil [THT, multilayer]"]
  C4 = Electrolytic Capacitor [capacitance=1µF package="100 mil [THT, electrolytic]"]
  R6 = Resistor [tolerance=±5% resistance=100k package=THT]

nets:
  N1: Q1.E, Q2.B
  N2: Q1.B, R1.Pin_1, C1.+
  N3: Q1.C, D1.cathode, R2.Pin_1
  N4: Q2.E, D1.anode, R5.Pin_0
  N5: Q2.C, R3.Pin_1, R4.Pin_0, C2.+
  N6: R1.Pin_0, R2.Pin_0, R3.Pin_0, C3.0, C4.+
  N7: C1.-, R6.Pin_0
  N8: R4.Pin_1, R5.Pin_1, C3.1, C4.-, R6.Pin_1

notes:
  IN
  OUT
  GND
  +15V
  GND
  NC
