# Fritzing sketch Cascode (saved by Fritzing 0.9.3b)
breadboards: 1

parts:
  Q1 = NPN-Transistor [package="TO92 [THT]"]
  Q2 = NPN-Transistor [package="TO92 [THT]"]
  R1 = Resistor [tolerance=±5% resistance=2k package=THT]
  R2 = Resistor [tolerance=±5% resistance=100k package=THT]
  C1 = Ceramic Capacitor [capacitance=100nF package="100 mil [THT, multilayer]"]
  R3 = Resistor [tolerance=±5% resistance=56k package=THT]
  C2 = Electrolytic Capacitor [capacitance=1µF package="100 mil [THT, electrolytic]"]
  C3 = Electrolytic Capacitor [capacitance=1µF package="100 mil [THT, electrolytic]"]
  R4 = Resistor [tolerance=±5% resistance=100k package=THT]
  R5 = Resistor [tolerance=±5% resistance=22k package=THT]
  C4 = Electrolytic Capacitor [capacitance=1µF package="100 mil [THT, electrolytic]"]
  R6 = Resistor [tolerance=±5% resistance=200 package=THT]
  R7 = Resistor [tolerance=±5% resistance=820 package=THT]
  C5 = Ceramic Capacitor [capacitance=100nF package="100 mil [THT, multilayer]"]
  C6 = Electrolytic Capacitor [capacitance=1µF package="100 mil [THT, electrolytic]"]
  C7 = Ceramic Capacitor [capacitance=100nF package="100 mil [THT, multilayer]"]
  C8 = Electrolytic Capacitor [capacitance=1µF package="100 mil [THT, electrolytic]"]
  R8 = Resistor [tolerance=±5% resistance=100k package=THT]

nets:
  N1: Q1.E, R6.Pin_0
  N2: Q1.B, Q2.E
  N3: Q1.C, R4.Pin_1, R5.Pin_0, C4.+
  N4: Q2.B, R1.Pin_1, C3.+
  N5: Q2.C, R2.Pin_1, C1.1, R3.Pin_0, C2.+
  N6: R1.Pin_0, R2.Pin_0, R4.Pin_0, C7.0, C8.+
  N7: C1.0, R3.Pin_1, C2.-, R5.Pin_1, R7.Pin_1, C5.0, C6.-, C7.1, C8.-, R8.Pin_1
  N8: C3.-, R8.Pin_0
  N9: R6.Pin_1, R7.Pin_0, C5.1, C6.+

notes:
  OUT
  IN
  GND
  +15V
  GND
  NC
