# Fritzing sketch CurrentMirror1_sine (saved by Fritzing 0.9.3b)
breadboards: 1
perfboards: 2

parts:
  Q1 = NPN-Transistor [package="TO92 [THT]"]
  Q2 = NPN-Transistor [package="TO92 [THT]"]
  R1 = Resistor [tolerance=±5% resistance=1k package=THT]
  J1 = female pin header, 2 pins [form="♀ (female)"]
  J2 = female pin header, 2 pins [form="♀ (female)"]
  J3 = female pin header, 2 pins [form="♀ (female)"]  # not connected
  Power_plug1 = Power plug
  C1 = Electrolytic Capacitor [capacitance=1µF package="100 mil [THT, electrolytic]"]

nets:
  N1: Q1.E, Q2.E, J1.pin1, J2.pin1, Power_plug1.GND, C1.-
  N2: Q1.B, Q1.C, Q2.C, J1.pin2
  N3: Q2.B, R1.Pin_0
  N4: R1.Pin_1, J2.pin2, Power_plug1.VCC, C1.+

notes:
  2SC1815
  E/C/B
  GND
  VCC
  VOUT
  VCCS
  DC5V
  AD9833
  Function Generator
