# Fritzing sketch CurrentMirror2 (saved by Fritzing 0.9.3b)
breadboards: 1
perfboards: 1

parts:
  Q1 = NPN-Transistor [package="TO92 [THT]"]
  Q2 = NPN-Transistor [package="TO92 [THT]"]
  R1 = Resistor [tolerance=±5% resistance=1k package=THT]
  R2 = Rotary Potentiometer (Small) [maximum_resistance=100kΩ package=THT]
  J1 = female pin header, 2 pins [form="♀ (female)"]
  J2 = female pin header, 2 pins [form="♀ (female)"]
  J3 = female pin header, 2 pins [form="♀ (female)"]
  Power_plug1 = Power plug
  J4 = female pin header, 2 pins [form="♀ (female)"]
  Q3 = NPN-Transistor [package="TO92 [THT]"]
  C1 = Electrolytic Capacitor [capacitance=1µF package="100 mil [THT, electrolytic]"]

nets:
  N1: Q1.E, Q2.E, J1.pin1, J4.pin1, C1.-
  N2: Q1.B, J1.pin2, Q3.C
  N3: Q1.C, Q2.C, Q3.E
  N4: Q2.B, R1.Pin_0
  N5: R1.Pin_1, J4.pin2, Q3.B, C1.+
  N6: R2.leg1, J2.pin1, Power_plug1.GND
  N7: R2.wiper, J3.pin1
  N8: R2.leg2, J2.pin2, Power_plug1.VCC

notes:
  2SC1815
  E/C/B
  GND
  VCC
  VOUT
  VCCS
  DC5V
