# Fritzing sketch Push-Pull (saved by Fritzing 0.9.3b)
breadboards: 1

parts:
  Q1 = PNP-Transistor [package="TO92 [THT]"]
  Q2 = NPN-Transistor [package="TO92 [THT]"]
  C1 = Electrolytic Capacitor [capacitance=1µF package="100 mil [THT, electrolytic]"]
  R1 = Resistor [tolerance=±1% resistance=4.7k package=THT]
  R2 = Resistor [tolerance=±1% resistance=4.7k package=THT]
  C2 = Electrolytic Capacitor [capacitance=1µF package="100 mil [THT, electrolytic]"]
  R3 = Resistor [tolerance=±1% resistance=1k package=THT]
  C3 = Electrolytic Capacitor [capacitance=1µF package="100 mil [THT, electrolytic]"]
  C4 = Ceramic Capacitor [capacitance=100nF package="100 mil [THT, multilayer]"]

nets:
  N1: Q1.E, Q2.E, C2.+
  N2: Q1.B, C1.-, R2.Pin_1, R3.Pin_1, C3.-, C4.1
  N3: Q1.C, Q2.C, C1.+, R1.Pin_1, R2.Pin_0
  N4: Q2.B, R1.Pin_0, C3.+, C4.0
  N5: C2.-, R3.Pin_0

notes:
  IN
  GND
  +9V
  GND
  NC
  OUT
