# Fritzing sketch Push-Pull_Diode_Bias (saved by Fritzing 0.9.3b)
breadboards: 1

parts:
  Q1 = PNP-Transistor [package="TO92 [THT]"]
  Q2 = NPN-Transistor [package="TO92 [THT]"]
  C1 = Electrolytic Capacitor [capacitance=1µF package="100 mil [THT, electrolytic]"]
  R1 = Resistor [tolerance=±1% resistance=4.7k package=THT]
  R2 = Resistor [tolerance=±1% resistance=4.7k package=THT]
  C2 = Electrolytic Capacitor [capacitance=1µF package="100 mil [THT, electrolytic]"]
  R3 = Resistor [tolerance=±1% resistance=1k package=THT]
  C3 = Electrolytic Capacitor [capacitance=1µF package="100 mil [THT, electrolytic]"]
  C4 = Ceramic Capacitor [capacitance=100nF package="100 mil [THT, multilayer]"]
  D1 = Rectifier Diode [part_number=1N4001 package="300 mil [THT]"]
  D2 = Rectifier Diode [part_number=1N4001 package="300 mil [THT]"]

nets:
  N1: Q1.E, Q2.E, C2.+
  N2: Q1.B, C1.-, R2.Pin_1, R3.Pin_1, C3.-, C4.1
  N3: Q1.C, R2.Pin_0, D2.cathode
  N4: Q2.B, R1.Pin_0, C3.+, C4.0
  N5: Q2.C, R1.Pin_1, D1.anode
  N6: C1.+, D1.cathode, D2.anode
  N7: C2.-, R3.Pin_0

notes:
  IN
  GND
  +9V
  GND
  NC
  OUT
