# Fritzing sketch Push-Pull_Diodex2_Bias (saved by Fritzing 0.9.3b)
breadboards: 1

parts:
  Q1 = PNP-Transistor [package="TO92 [THT]"]
  Q2 = NPN-Transistor [package="TO92 [THT]"]
  C1 = Electrolytic Capacitor [capacitance=1µF package="100 mil [THT, electrolytic]"]
  R1 = Resistor [tolerance=±1% resistance=8.2k package=THT]
  R2 = Resistor [tolerance=±1% resistance=8.2k package=THT]
  C2 = Electrolytic Capacitor [capacitance=1µF package="100 mil [THT, electrolytic]"]
  R3 = Resistor [tolerance=±1% resistance=1k package=THT]
  C3 = Electrolytic Capacitor [capacitance=1µF package="100 mil [THT, electrolytic]"]
  C4 = Ceramic Capacitor [capacitance=100nF package="100 mil [THT, multilayer]"]
  D1 = Rectifier Diode [part_number=1N4001 package="300 mil [THT]"]
  D2 = Rectifier Diode [part_number=1N4001 package="300 mil [THT]"]
  D3 = Rectifier Diode [part_number=1N4001 package="300 mil [THT]"]
  D4 = Rectifier Diode [part_number=1N4001 package="300 mil [THT]"]
  R4 = Resistor [tolerance=±5% resistance=100 package=THT]
  R5 = Resistor [tolerance=±5% resistance=100 package=THT]

nets:
  N1: Q1.E, R5.Pin_1
  N2: Q1.B, C1.-, R2.Pin_1, C2.-, R3.Pin_0, R3.Pin_1, C3.-, C4.1
  N3: Q1.C, R2.Pin_0, D2.cathode
  N4: Q2.E, R4.Pin_1
  N5: Q2.B, R1.Pin_0, C3.+, C4.0
  N6: Q2.C, R1.Pin_1, D1.anode
  N7: C1.+, D3.cathode, D4.anode
  N8: C2.+, R4.Pin_0, R5.Pin_0
  N9: D1.cathode, D3.anode
  N10: D2.anode, D4.cathode

notes:
  IN
  GND
  +9V
  GND
  NC
  OUT
