# Fritzing sketch DiamondBuffer (saved by Fritzing 0.9.3b)
breadboards: 1

parts:
  Q1 = NPN-Transistor [package="TO92 [THT]"]
  Q2 = PNP-Transistor [package="TO92 [THT]"]
  C1 = Ceramic Capacitor [capacitance=100nF package="100 mil [THT, multilayer]"]
  C2 = Ceramic Capacitor [capacitance=100nF package="100 mil [THT, multilayer]"]
  Q3 = PNP-Transistor [package="TO92 [THT]"]
  R1 = Resistor [tolerance=±5% resistance=3.3k package=THT]
  Q4 = NPN-Transistor [package="TO92 [THT]"]
  R2 = Resistor [tolerance=±5% resistance=3.3k package=THT]
  R3 = Resistor [tolerance=±5% resistance=100 package=THT]
  C3 = Electrolytic Capacitor [capacitance=1µF package="100 mil [THT, electrolytic]"]
  C4 = Electrolytic Capacitor [capacitance=1µF package="100 mil [THT, electrolytic]"]
  R4 = Resistor [tolerance=±5% resistance=100k package=THT]
  R5 = Resistor [tolerance=±5% resistance=100 package=THT]

nets:
  N1: Q1.E, Q2.E, R5.Pin_1
  N2: Q1.B, C1.0, R1.Pin_0, Q4.B, C3.+
  N3: Q1.C, Q3.E, R1.Pin_1
  N4: Q2.B, C2.1, Q3.B, R2.Pin_1, C4.-
  N5: Q2.C, Q4.E, R2.Pin_0
  N6: C1.1, C2.0, C3.-, C4.+, R4.Pin_1, R5.Pin_0
  N7: Q3.C, Q4.C, R3.Pin_0
  N8: R3.Pin_1, R4.Pin_0

notes:
  GND
  +4.5V
  -4.5V
  GND
  IN
  OUT
