# Fritzing sketch BaseCommon (saved by Fritzing 0.9.3b)
breadboards: 1

parts:
  Q1 = NPN-Transistor [package="TO92 [THT]"]
  R1 = Resistor [tolerance=±5% resistance=1k package=THT]
  R2 = Resistor [tolerance=±5% resistance=1k package=THT]
  C1 = Electrolytic Capacitor [capacitance=1µF package="100 mil [THT, electrolytic]"]
  R3 = Resistor [tolerance=±5% resistance=27k package=THT]
  R4 = Resistor [tolerance=±5% resistance=68k package=THT]
  R5 = Resistor [tolerance=±5% resistance=4.7k package=THT]
  C3 = Ceramic Capacitor [capacitance=100nF package="100 mil [THT, multilayer]"]
  C4 = Electrolytic Capacitor [capacitance=1µF package="100 mil [THT, electrolytic]"]
  R6 = Resistor [tolerance=±5% resistance=100k package=THT]
  C5 = Electrolytic Capacitor [capacitance=1µF package="100 mil [THT, electrolytic]"]
  C6 = Electrolytic Capacitor [capacitance=1µF package="100 mil [THT, electrolytic]"]

nets:
  N1: Q1.E, R1.Pin_1
  N2: Q1.B, R5.Pin_1, C4.+
  N3: Q1.C, R3.Pin_0, R4.Pin_1, C6.+
  N4: R1.Pin_0, R2.Pin_0, C1.+
  N5: R2.Pin_1, R3.Pin_1, C3.0, R6.Pin_0, C5.-, C6.-
  N6: R4.Pin_0, R5.Pin_0, C3.1, C5.+
  N7: C4.-, R6.Pin_1

notes:
  GND
  NC
  IN
  GND
  VCC
  OUT
