# Fritzing sketch Diff_amp (saved by Fritzing 0.9.3b)
breadboards: 1

parts:
  Q1 = NPN-Transistor [package="TO92 [THT]"]
  Q2 = NPN-Transistor [package="TO92 [THT]"]
  Q3 = NPN-Transistor [package="TO92 [THT]"]
  R1 = Resistor [tolerance=±5% resistance=2.2k package=THT]
  R2 = Resistor [tolerance=±5% resistance=2.2k package=THT]
  R3 = Resistor [tolerance=±5% resistance=1k package=THT]
  R4 = Resistor [tolerance=±5% resistance=12k package=THT]
  R5 = Resistor [tolerance=±5% resistance=33k package=THT]
  R6 = Resistor [tolerance=±5% resistance=10k package=THT]
  R7 = Resistor [tolerance=±5% resistance=10k package=THT]
  C1 = Electrolytic Capacitor [capacitance=1µF package="100 mil [THT, electrolytic]"]
  C2 = Electrolytic Capacitor [capacitance=1µF package="100 mil [THT, electrolytic]"]
  R8 = Resistor [tolerance=±5% resistance=100k package=THT]
  R9 = Resistor [tolerance=±5% resistance=100k package=THT]
  C3 = Electrolytic Capacitor [capacitance=1µF package="100 mil [THT, electrolytic]"]
  C4 = Electrolytic Capacitor [capacitance=1µF package="100 mil [THT, electrolytic]"]
  C5 = Ceramic Capacitor [capacitance=100nF package="100 mil [THT, multilayer]"]
  C6 = Ceramic Capacitor [capacitance=100nF package="100 mil [THT, multilayer]"]
  C7 = Ceramic Capacitor [capacitance=100nF package="100 mil [THT, multilayer]"]

nets:
  N1: Q1.E, Q2.E, Q3.B
  N2: Q1.B, R2.Pin_1, C1.+
  N3: Q1.C, R6.Pin_1
  N4: Q2.B, R1.Pin_1, C2.+
  N5: Q2.C, R7.Pin_1
  N6: Q3.E, R3.Pin_0
  N7: Q3.C, R4.Pin_0, R5.Pin_0
  N8: R1.Pin_0, R2.Pin_0, R5.Pin_1, C4.+, C5.0, C6.0
  N9: R3.Pin_1, R4.Pin_1, C3.-, C7.0
  N10: R6.Pin_0, R7.Pin_0, R8.Pin_0, R9.Pin_0, C3.+, C4.-, C5.1, C6.1, C7.1
  N11: C1.-, R8.Pin_1
  N12: C2.-, R9.Pin_1

notes:
  VEE
  GND
  GND
  VCC
  IN1
  IN2
  OUT1
  OUT2
