# Fritzing sketch Diff_amp_CurrentSource (saved by Fritzing 0.9.3b)
breadboards: 1
perfboards: 2

parts:
  Q1 = NPN-Transistor [package="TO92 [THT]"]
  Q2 = NPN-Transistor [package="TO92 [THT]"]
  R1 = Resistor [tolerance=±5% resistance=2.2k package=THT]
  R2 = Resistor [tolerance=±5% resistance=2.2k package=THT]
  R6 = Resistor [tolerance=±5% resistance=10k package=THT]
  R7 = Resistor [tolerance=±5% resistance=10k package=THT]
  C1 = Electrolytic Capacitor [capacitance=1µF package="100 mil [THT, electrolytic]"]
  C2 = Electrolytic Capacitor [capacitance=1µF package="100 mil [THT, electrolytic]"]
  R8 = Resistor [tolerance=±5% resistance=100k package=THT]
  R9 = Resistor [tolerance=±5% resistance=100k package=THT]
  C4 = Electrolytic Capacitor [capacitance=1µF package="100 mil [THT, electrolytic]"]
  C5 = Ceramic Capacitor [capacitance=100nF package="100 mil [THT, multilayer]"]
  C6 = Ceramic Capacitor [capacitance=100nF package="100 mil [THT, multilayer]"]
  R10 = Rotary Potentiometer (Small) [maximum_resistance=100kΩ package=THT]

nets:
  N1: Q1.E, Q2.E
  N2: Q1.B, R2.Pin_1, C1.+
  N3: Q1.C, R6.Pin_1
  N4: Q2.B, R1.Pin_1, C2.+
  N5: Q2.C, R7.Pin_1
  N6: R1.Pin_0, R2.Pin_0, C4.+, C5.0, C6.0
  N7: R6.Pin_0, R7.Pin_0, R8.Pin_0, R9.Pin_0, C4.-, C5.1, C6.1, R10.leg2
  N8: C1.-, R8.Pin_1
  N9: C2.-, R9.Pin_1

notes:
  VEE
  GND
  GND
  VCC
  IN1
  IN2
  OUT1
  OUT2
  Current
  Source
