# Fritzing sketch NegativeFeedback_r2 (saved by Fritzing 0.9.3b)
breadboards: 1

parts:
  Q1 = NPN-Transistor [package="TO92 [THT]"]
  Q2 = PNP-Transistor [package="TO92 [THT]"]
  R1 = Resistor [tolerance=±5% resistance=5.6k package=THT]
  R2 = Resistor [tolerance=±5% resistance=100 package=THT]
  R3 = Resistor [tolerance=±5% resistance=2.0k package=THT]
  C1 = Electrolytic Capacitor [capacitance=0.1mF package="100 mil [THT, electrolytic]"]
  C2 = Electrolytic Capacitor [capacitance=10µF package="100 mil [THT, electrolytic]"]
  R5 = Resistor [tolerance=±5% resistance=150k package=THT]
  R6 = Resistor [tolerance=±5% resistance=33k package=THT]
  C3 = Electrolytic Capacitor [capacitance=10µF package="100 mil [THT, electrolytic]"]
  R7 = Resistor [tolerance=±5% resistance=1.5k package=THT]
  C4 = Electrolytic Capacitor [capacitance=0.1mF package="100 mil [THT, electrolytic]"]
  R8 = Resistor [tolerance=±5% resistance=1.5k package=THT]
  C5 = Electrolytic Capacitor [capacitance=10µF package="100 mil [THT, electrolytic]"]
  R9 = Resistor [tolerance=±5% resistance=100k package=THT]
  C6 = Ceramic Capacitor [capacitance=100nF package="100 mil [THT, multilayer]"]
  C7 = Electrolytic Capacitor [capacitance=0.1mF package="100 mil [THT, electrolytic]"]
  R10 = Resistor [tolerance=±5% resistance=10k package=THT]
  R11 = Resistor [tolerance=±5% resistance=200 package=THT]
  R12 = Resistor [tolerance=±5% resistance=1.8k package=THT]

nets:
  N1: Q1.E, R2.Pin_0
  N2: Q1.B, Q2.C, R1.Pin_0
  N3: Q1.C, R5.Pin_1, R6.Pin_0, C3.+
  N4: Q2.E, R7.Pin_1, C4.-
  N5: Q2.B, C2.+, R8.Pin_0, C5.+
  N6: R1.Pin_1, R5.Pin_0, R7.Pin_0, C4.+, C6.1, C7.+
  N7: R2.Pin_1, R3.Pin_0, C1.+, R10.Pin_1
  N8: R3.Pin_1, C1.-, R6.Pin_1, R8.Pin_1, R9.Pin_1, C6.0, C7.-, R11.Pin_0
  N9: C2.-, R10.Pin_0
  N10: C3.-, R11.Pin_1, R12.Pin_0
  N11: C5.-, R9.Pin_0

notes:
  IN
  OUT
  GND
  15V
  1/10
